// Logisim project 16bit ALU.circ as structural Verilog
module main (
  input  Cin,
  input  [7:0] A,
  input  [7:0] B,
  input  Bin,
  input  [1:0] Opcode,
  input  Cin_2,
  input  [15:0] A_2,
  input  [15:0] B_2,
  input  Bin_2,
  input  [1:0] Opcode_2,
  output out_11,
  output [7:0] out_12,
  output out_13,
  output out_14,
  output [15:0] out_15,
  output out_16,
  output out_17,
  output out_18
);

  _8bit_ALU u_8bit_alu_1 ();
  // _16bit_ALU 16bit_alu_1: pin names not known; wires that end beside it: A_2, B_2, Cin_2, out_15, out_16, out_17
endmodule

module ALU (
  input  Cin,
  input  A,
  input  [1:0] ALUop,
  input  B,
  input  Bin,
  output Result,
  output Cout
);

  wire adder_1_out, and_1_out, multiplexer_1_out, not_1_out, or_1_out;

  Multiplexer #(.enable("false")) multiplexer_1 (.in0(B), .in1(not_1_out), .out(multiplexer_1_out), .sel(Bin));
  not not_1 (not_1_out, B);
  Adder #(.width(1)) adder_1 (.a(A), .b(multiplexer_1_out), .out(adder_1_out), .cin(Cin), .cout(Cout));
  and and_1 (and_1_out, A, multiplexer_1_out);
  or or_1 (or_1_out, A, multiplexer_1_out);
  Multiplexer #(.select(2), .enable("false")) multiplexer_2 (
    .in0(and_1_out), .in1(or_1_out), .in2(adder_1_out), .out(Result), .sel(ALUop));  // open: in3
endmodule

module _16bit_ALU (
  input  in_1,
  input  [15:0] A,
  input  [1:0] in_3,
  input  in_4,
  output out_5,
  output [15:0] out_6,
  output out_7
);

  wire comparator_1_eq;
  wire [3:0] bit_extender_1_out;
  wire [15:0] adder_1_out, and_1_out, bit_extender_2_out, multiplexer_1_out, not_1_out, shifter_1_out,
       undriven;

  Multiplexer #(.width(16), .enable("false")) multiplexer_1 (
    .in0(undriven), .in1(not_1_out), .out(multiplexer_1_out), .sel(in_4));
  assign not_1_out = ~undriven;  // NOT_Gate not_1, 16 bits wide
  Comparator #(.width(16)) comparator_1 (.a(A), .b(multiplexer_1_out), .eq(comparator_1_eq));  // open: gt, lt
  Bit_Extender #(.in_width(16), .out_width(4)) bit_extender_1 (.in(multiplexer_1_out), .out(bit_extender_1_out));
  Adder #(.width(16)) adder_1 (.a(A), .b(multiplexer_1_out), .out(adder_1_out), .cin(in_1), .cout(out_5));
  Shifter #(.width(16)) shifter_1 (.in(A), .\dist (bit_extender_1_out), .out(shifter_1_out));
  assign bit_extender_2_out = {{15{1'b0}}, comparator_1_eq};  // Bit_Extender bit_extender_2
  assign and_1_out = A & multiplexer_1_out;  // AND_Gate and_1, 16 bits wide
  Multiplexer #(.select(2), .width(16), .enable("false")) multiplexer_2 (
    .in0(adder_1_out), .in1(shifter_1_out), .in2(bit_extender_2_out), .in3(and_1_out), .out(out_6), .sel(in_3));
  nor nor_1 (out_7, out_6[0], out_6[1], out_6[2], out_6[3], out_6[4], out_6[5], out_6[6], out_6[7], out_6[8], out_6[9], out_6[10], out_6[11], out_6[12], out_6[13], out_6[14], out_6[15]);
endmodule

module _16bit_Register (
  input  [15:0] Write_Data,
  input  [3:0] ReadReg1,
  input  RegWriteEN,
  input  [3:0] Write_Select,
  input  [3:0] ReadRg2,
  input  CLK,
  output [15:0] ReadData1,
  output [15:0] ReadData2
);

  wire decoder_1_out0, decoder_1_out1, decoder_1_out2, decoder_1_out3, decoder_1_out4, decoder_1_out5,
       decoder_1_out6, decoder_1_out7, decoder_1_out8, decoder_1_out9, decoder_1_out10, decoder_1_out11,
       decoder_1_out12, decoder_1_out13, decoder_1_out14, decoder_1_out15;
  wire [15:0] register_1_q, register_2_q, register_3_q, register_4_q, register_5_q, register_6_q,
       register_7_q, register_8_q, register_9_q, register_10_q, register_11_q, register_12_q, register_13_q,
       register_14_q, register_15_q, register_16_q;

  Decoder #(.select(4)) decoder_1 (
    .out0(decoder_1_out0), .out1(decoder_1_out1), .out2(decoder_1_out2), .out3(decoder_1_out3),
    .out4(decoder_1_out4), .out5(decoder_1_out5), .out6(decoder_1_out6), .out7(decoder_1_out7),
    .out8(decoder_1_out8), .out9(decoder_1_out9), .out10(decoder_1_out10), .out11(decoder_1_out11),
    .out12(decoder_1_out12), .out13(decoder_1_out13), .out14(decoder_1_out14), .out15(decoder_1_out15),
    .sel(Write_Select), .en(RegWriteEN));
  Register #(.width(16)) register_1 (.D(Write_Data), .en(decoder_1_out0), .Q(register_1_q), .clk(CLK));  // open: clr
  Register #(.width(16)) register_2 (.D(Write_Data), .en(decoder_1_out1), .Q(register_2_q), .clk(CLK));  // open: clr
  Register #(.width(16)) register_3 (.D(Write_Data), .en(decoder_1_out2), .Q(register_3_q), .clk(CLK));  // open: clr
  Register #(.width(16)) register_4 (.D(Write_Data), .en(decoder_1_out3), .Q(register_4_q), .clk(CLK), .clr(CLK));
  Register #(.width(16)) register_5 (.D(Write_Data), .en(decoder_1_out4), .Q(register_5_q), .clk(CLK));  // open: clr
  Register #(.width(16)) register_6 (.D(Write_Data), .en(decoder_1_out5), .Q(register_6_q), .clk(CLK));  // open: clr
  Register #(.width(16)) register_7 (.D(Write_Data), .en(decoder_1_out6), .Q(register_7_q), .clk(CLK));  // open: clr
  Register #(.width(16)) register_8 (.D(Write_Data), .en(decoder_1_out7), .Q(register_8_q), .clk(CLK));  // open: clr
  Register #(.width(16)) register_9 (.D(Write_Data), .en(decoder_1_out8), .Q(register_9_q), .clk(CLK));  // open: clr
  Register #(.width(16)) register_10 (.D(Write_Data), .en(decoder_1_out9), .Q(register_10_q), .clk(CLK));  // open: clr
  Register #(.width(16)) register_11 (.D(Write_Data), .en(decoder_1_out10), .Q(register_11_q), .clk(CLK));  // open: clr
  Register #(.width(16)) register_12 (.D(Write_Data), .en(decoder_1_out11), .Q(register_12_q), .clk(CLK));  // open: clr
  Register #(.width(16)) register_13 (.D(Write_Data), .en(decoder_1_out12), .Q(register_13_q), .clk(CLK));  // open: clr
  Register #(.width(16)) register_14 (.D(Write_Data), .en(decoder_1_out13), .Q(register_14_q), .clk(CLK));  // open: clr
  Register #(.width(16)) register_15 (.D(Write_Data), .en(decoder_1_out14), .Q(register_15_q), .clk(CLK));  // open: clr
  Register #(.width(16)) register_16 (.D(Write_Data), .en(decoder_1_out15), .Q(register_16_q), .clk(CLK));  // open: clr
  Multiplexer #(.select(4), .width(16), .enable("false")) multiplexer_1 (
    .in0(register_1_q), .in1(register_2_q), .in2(register_3_q), .in3(register_4_q), .in4(register_5_q),
    .in5(register_6_q), .in6(register_7_q), .in7(register_8_q), .in8(register_9_q), .in9(register_10_q),
    .in10(register_11_q), .in11(register_12_q), .in12(register_13_q), .in13(register_14_q),
    .in14(register_15_q), .in15(register_16_q), .out(ReadData1), .sel(ReadReg1));
  Multiplexer #(.select(4), .width(16), .enable("false")) multiplexer_2 (
    .in0(register_1_q), .in1(register_2_q), .in2(register_3_q), .in3(register_4_q), .in4(register_5_q),
    .in5(register_6_q), .in6(register_7_q), .in7(register_8_q), .in8(register_9_q), .in9(register_10_q),
    .in10(register_11_q), .in11(register_12_q), .in12(register_13_q), .in13(register_14_q),
    .in14(register_15_q), .in15(register_16_q), .out(ReadData2), .sel(ReadRg2));
endmodule

module DataPath (
  input  in_1,
  input  in_2,
  input  RT_IM,
  input  in_4,
  input  in_5,
  input  [1:0] in_6,
  output [3:0] Rd,
  output [15:0] out_8,
  output [3:0] Opcode,
  output [3:0] Rs,
  output out_11,
  output [3:0] Rt_Im_2,
  output out_13
);

  wire clock_1_out, clock_2_out;
  wire [15:0] adder_1_out, bit_extender_1_out, counter_1_q, multiplexer_1_out, multiplexer_2_out,
       n16bit_register_1_readdata1, n16bit_register_1_readdata2, ram_1_data, undriven;

  Clock clock_1 (.out(clock_1_out));
  Counter #(.width(16), .max('hffff)) counter_1 (
    .D(adder_1_out), .Q(counter_1_q), .clk(clock_1_out));  // open: load, count, carry, clr
  Control_Unit control_unit_1 (.in_1(Opcode));  // open: RegWriteEn, RT_Im, Op, MEMToReq, Branch, Jmp, Lw, Sw, Cin_Bin
  Adder #(.width(16)) adder_1 (.a(counter_1_q), .b(16'h1), .out(adder_1_out), .cin(1'b0));  // open: cout
  ROM #(.addrWidth(16), .dataWidth(16)) rom_1 (.addr(counter_1_q), .data({Opcode, Rd, Rs, Rt_Im_2}));  // open: sel
  assign bit_extender_1_out = {{12{1'b0}}, Rt_Im_2};  // Bit_Extender bit_extender_1
  Clock clock_2 (.out(clock_2_out));
  _16bit_Register u_16bit_register_1 (
    .Write_Data(multiplexer_2_out), .ReadReg1(Rs), .ReadRg2(Rt_Im_2), .CLK(clock_2_out),
    .ReadData1(n16bit_register_1_readdata1), .ReadData2(n16bit_register_1_readdata2), .RegWriteEN(in_4));  // open: Write_Select
  Multiplexer #(.width(16), .enable("false")) multiplexer_1 (
    .in0(n16bit_register_1_readdata2), .in1(bit_extender_1_out), .out(multiplexer_1_out), .sel(RT_IM));
  RAM #(.addrWidth(16), .dataWidth(16), .bus("separate")) ram_1 (
    .addr(out_8), .din(undriven), .data(ram_1_data));  // open: str, sel, clk, ld, clr
  Multiplexer #(.width(16), .enable("false")) multiplexer_2 (
    .in0(out_8), .in1(ram_1_data), .out(multiplexer_2_out), .sel(in_5));
endmodule

module Control_Unit (
  input  [3:0] in_1,
  output RegWriteEn,
  output RT_Im,
  output Cin_Bin,
  output [1:0] Op,
  output MEMToReq,
  output Branch,
  output Jmp,
  output Lw,
  output Sw
);

  wire ADD0101_out, ADDI0001_out, AND0111_out, BEQ0000_out, SLL0100_out, SLT_0011_out, SUB0010_out;

  and BEQ0000 (BEQ0000_out, ~in_1[3], ~in_1[3], ~in_1[3], ~in_1[0]);  // AND_Gate
  and ADDI0001 (ADDI0001_out, ~in_1[3], ~in_1[3], ~in_1[3], in_1[0]);  // AND_Gate
  and SUB0010 (SUB0010_out, ~in_1[3], ~in_1[3], in_1[3], ~in_1[0]);  // AND_Gate
  and SLT_0011 (SLT_0011_out, ~in_1[3], ~in_1[3], in_1[3], in_1[0]);  // AND_Gate
  and SLL0100 (SLL0100_out, ~in_1[3], in_1[3], ~in_1[3], ~in_1[0]);  // AND_Gate
  and ADD0101 (ADD0101_out, ~in_1[3], in_1[3], ~in_1[3], in_1[0]);  // AND_Gate
  and LW0110 (Lw, ~in_1[3], in_1[3], in_1[3], ~in_1[0]);  // AND_Gate
  and AND0111 (AND0111_out, ~in_1[3], in_1[3], in_1[3], ~in_1[0]);  // AND_Gate
  and JMP1000 (Jmp, in_1[3], ~in_1[3], ~in_1[3], ~in_1[0]);  // AND_Gate
  and SW1001 (Sw, in_1[3], ~in_1[3], ~in_1[3], in_1[0]);  // AND_Gate
  or or_1 (RegWriteEn, ADDI0001_out, SUB0010_out, SLT_0011_out, SLL0100_out, ADD0101_out, AND0111_out, Sw);
  or or_2 (RT_Im, SLL0100_out, ADD0101_out, Lw, Jmp);
  or or_3 (Op[0], ADDI0001_out, SUB0010_out, SLT_0011_out, SLL0100_out, Lw, Sw);
  or or_4 (Op[1], ADDI0001_out, SUB0010_out, SLT_0011_out, SLL0100_out, Lw, Sw);
  or or_5 (Branch, BEQ0000_out, Jmp);
  or or_6 (Cin_Bin, SUB0010_out, SUB0010_out);

  assign in_1[2:1] = {2{in_1[3]}};
  assign MEMToReq = Lw;
endmodule

module ALU1 (
  input  in_1,
  input  [15:0] A,
  input  [1:0] in_3,
  input  in_4,
  output out_5,
  output [15:0] out_6,
  output out_7
);

  wire comparator_1_eq;
  wire [3:0] bit_extender_1_out;
  wire [15:0] adder_1_out, and_1_out, multiplexer_1_out, not_1_out, shifter_1_out, undriven;

  Multiplexer #(.width(16), .enable("false")) multiplexer_1 (
    .in0(undriven), .in1(not_1_out), .out(multiplexer_1_out), .sel(in_4));
  assign not_1_out = ~undriven;  // NOT_Gate not_1, 16 bits wide
  Comparator #(.width(16)) comparator_1 (.a(A), .b(multiplexer_1_out), .eq(comparator_1_eq));  // open: gt, lt
  Bit_Extender #(.in_width(16), .out_width(4)) bit_extender_1 (.in(multiplexer_1_out), .out(bit_extender_1_out));
  Adder #(.width(16)) adder_1 (.a(A), .b(multiplexer_1_out), .out(adder_1_out), .cin(in_1), .cout(out_5));
  Shifter #(.width(16)) shifter_1 (.in(A), .\dist (bit_extender_1_out), .out(shifter_1_out));
  assign shifter_1_out = {{15{1'b0}}, comparator_1_eq};  // Bit_Extender bit_extender_2
  assign and_1_out = A & multiplexer_1_out;  // AND_Gate and_1, 16 bits wide
  Multiplexer #(.select(2), .width(16), .enable("false")) multiplexer_2 (
    .in0(adder_1_out), .in1(shifter_1_out), .in2(shifter_1_out), .in3(and_1_out), .out(out_6), .sel(in_3));
  nor nor_1 (out_7, out_6[0], out_6[1], out_6[2], out_6[3], out_6[4], out_6[5], out_6[6], out_6[7], out_6[8], out_6[9], out_6[10], out_6[11], out_6[12], out_6[13], out_6[14], out_6[15]);
endmodule
