// Logisim project Project.circ as structural Verilog: 5 circuits, main circuit main
module main (
  input  in_1,
  input  [15:0] A,
  input  [1:0] in_3,
  input  [15:0] B,
  input  in_5,
  output out_6,
  output [15:0] out_7,
  output out_8
);

  wire comparator_1_eq;
  wire [3:0] bit_extender_1_out;
  wire [15:0] adder_1_out, and_1_out, bit_extender_2_out, multiplexer_1_out, not_1_out, shifter_1_out;

  Multiplexer #(.width(16), .enable("false")) multiplexer_1 (
    .in0(B), .in1(not_1_out), .out(multiplexer_1_out), .sel(in_5));
  assign not_1_out = ~B;  // NOT_Gate not_1, 16 bits wide
  Comparator #(.width(16)) comparator_1 (.a(A), .b(multiplexer_1_out), .eq(comparator_1_eq));  // open: gt, lt
  Bit_Extender #(.in_width(16), .out_width(4)) bit_extender_1 (.in(multiplexer_1_out), .out(bit_extender_1_out));
  Adder #(.width(16)) adder_1 (.a(A), .b(multiplexer_1_out), .out(adder_1_out), .cin(in_1), .cout(out_6));
  Shifter #(.width(16)) shifter_1 (.in(A), .\dist (bit_extender_1_out), .out(shifter_1_out));
  assign bit_extender_2_out = {{15{1'b0}}, comparator_1_eq};  // Bit_Extender bit_extender_2
  assign and_1_out = A & multiplexer_1_out;  // AND_Gate and_1, 16 bits wide
  Multiplexer #(.select(2), .width(16), .enable("false")) multiplexer_2 (
    .in0(adder_1_out), .in1(shifter_1_out), .in2(bit_extender_2_out), .in3(and_1_out), .out(out_7), .sel(in_3));
  nor nor_1 (out_8, out_7[0], out_7[1], out_7[2], out_7[3], out_7[4], out_7[5], out_7[6], out_7[7], out_7[8], out_7[9], out_7[10], out_7[11], out_7[12], out_7[13], out_7[14], out_7[15]);
endmodule

module _16bit_ALU (
  input  Cin,
  input  [15:0] A,
  input  [1:0] Opcode,
  input  [15:0] B,
  input  Bin,
  output Cout,
  output [15:0] Result,
  output Zero
);

  wire comparator_1_eq;
  wire [3:0] bit_extender_1_out;
  wire [15:0] adder_1_out, and_1_out, bit_extender_2_out, multiplexer_1_out, not_1_out, shifter_1_out;

  Multiplexer #(.width(16), .enable("false")) multiplexer_1 (
    .in0(B), .in1(not_1_out), .out(multiplexer_1_out), .sel(Bin));
  assign not_1_out = ~B;  // NOT_Gate not_1, 16 bits wide
  Comparator #(.width(16)) comparator_1 (.a(A), .b(multiplexer_1_out), .eq(comparator_1_eq));  // open: gt, lt
  Bit_Extender #(.in_width(16), .out_width(4)) bit_extender_1 (.in(multiplexer_1_out), .out(bit_extender_1_out));
  Adder #(.width(16)) adder_1 (.a(A), .b(multiplexer_1_out), .out(adder_1_out), .cin(Cin), .cout(Cout));
  Shifter #(.width(16)) shifter_1 (.in(A), .\dist (bit_extender_1_out), .out(shifter_1_out));
  assign bit_extender_2_out = {{15{1'b0}}, comparator_1_eq};  // Bit_Extender bit_extender_2
  assign and_1_out = A & multiplexer_1_out;  // AND_Gate and_1, 16 bits wide
  Multiplexer #(.select(2), .width(16), .enable("false")) multiplexer_2 (
    .in0(adder_1_out), .in1(shifter_1_out), .in2(bit_extender_2_out), .in3(and_1_out), .out(Result),
    .sel(Opcode));
  nor nor_1 (Zero, Result[0], Result[1], Result[2], Result[3], Result[4], Result[5], Result[6], Result[7], Result[8], Result[9], Result[10], Result[11], Result[12], Result[13], Result[14], Result[15]);
endmodule

module _16bit_Register (
  input  [15:0] Write_Data,
  input  [3:0] ReadReg1_Rs,
  input  RegWriteEN,
  input  [3:0] Write_Select_Rd,
  input  [3:0] ReadRg2_Rt,
  input  CLK,
  output [15:0] ReadData1,
  output [15:0] ReadData2
);

  wire decoder_1_out0, decoder_1_out1, decoder_1_out2, decoder_1_out3, decoder_1_out4, decoder_1_out5,
       decoder_1_out6, decoder_1_out7, decoder_1_out8, decoder_1_out9, decoder_1_out10, decoder_1_out11,
       decoder_1_out12, decoder_1_out13, decoder_1_out14, decoder_1_out15;
  wire [15:0] R0_q, R1_q, R2_q, R3_q, R4_q, R5_q, R6_q, R7_q, R8_q, R9_q, R10_q, R11_q, R12_q, R13_q, R14_q,
       R15_q;

  Decoder #(.select(4)) decoder_1 (
    .out0(decoder_1_out0), .out1(decoder_1_out1), .out2(decoder_1_out2), .out3(decoder_1_out3),
    .out4(decoder_1_out4), .out5(decoder_1_out5), .out6(decoder_1_out6), .out7(decoder_1_out7),
    .out8(decoder_1_out8), .out9(decoder_1_out9), .out10(decoder_1_out10), .out11(decoder_1_out11),
    .out12(decoder_1_out12), .out13(decoder_1_out13), .out14(decoder_1_out14), .out15(decoder_1_out15),
    .sel(Write_Select_Rd), .en(RegWriteEN));
  Register #(.width(16)) R0 (.D(Write_Data), .en(decoder_1_out0), .Q(R0_q), .clk(CLK));  // open: clr
  Register #(.width(16)) R1 (.D(Write_Data), .en(decoder_1_out1), .Q(R1_q), .clk(CLK));  // open: clr
  Register #(.width(16)) R2 (.D(Write_Data), .en(decoder_1_out2), .Q(R2_q), .clk(CLK));  // open: clr
  Register #(.width(16)) R3 (.D(Write_Data), .en(decoder_1_out3), .Q(R3_q), .clk(CLK), .clr(CLK));
  Register #(.width(16)) R4 (.D(Write_Data), .en(decoder_1_out4), .Q(R4_q), .clk(CLK));  // open: clr
  Register #(.width(16)) R5 (.D(Write_Data), .en(decoder_1_out5), .Q(R5_q), .clk(CLK));  // open: clr
  Register #(.width(16)) R6 (.D(Write_Data), .en(decoder_1_out6), .Q(R6_q), .clk(CLK));  // open: clr
  Register #(.width(16)) R7 (.D(Write_Data), .en(decoder_1_out7), .Q(R7_q), .clk(CLK));  // open: clr
  Register #(.width(16)) R8 (.D(Write_Data), .en(decoder_1_out8), .Q(R8_q), .clk(CLK));  // open: clr
  Register #(.width(16)) R9 (.D(Write_Data), .en(decoder_1_out9), .Q(R9_q), .clk(CLK));  // open: clr
  Register #(.width(16)) R10 (.D(Write_Data), .en(decoder_1_out10), .Q(R10_q), .clk(CLK));  // open: clr
  Register #(.width(16)) R11 (.D(Write_Data), .en(decoder_1_out11), .Q(R11_q), .clk(CLK));  // open: clr
  Register #(.width(16)) R12 (.D(Write_Data), .en(decoder_1_out12), .Q(R12_q), .clk(CLK));  // open: clr
  Register #(.width(16)) R13 (.D(Write_Data), .en(decoder_1_out13), .Q(R13_q), .clk(CLK));  // open: clr
  Register #(.width(16)) R14 (.D(Write_Data), .en(decoder_1_out14), .Q(R14_q), .clk(CLK));  // open: clr
  Register #(.width(16)) R15 (.D(Write_Data), .en(decoder_1_out15), .Q(R15_q), .clk(CLK));  // open: clr
  Multiplexer #(.select(4), .width(16), .enable("false")) multiplexer_1 (
    .in0(R0_q), .in1(R1_q), .in2(R2_q), .in3(R3_q), .in4(R4_q), .in5(R5_q), .in6(R6_q), .in7(R7_q),
    .in8(R8_q), .in9(R9_q), .in10(R10_q), .in11(R11_q), .in12(R12_q), .in13(R13_q), .in14(R14_q),
    .in15(R15_q), .out(ReadData1), .sel(ReadReg1_Rs));
  Multiplexer #(.select(4), .width(16), .enable("false")) multiplexer_2 (
    .in0(R0_q), .in1(R1_q), .in2(R2_q), .in3(R3_q), .in4(R4_q), .in5(R5_q), .in6(R6_q), .in7(R7_q),
    .in8(R8_q), .in9(R9_q), .in10(R10_q), .in11(R11_q), .in12(R12_q), .in13(R13_q), .in14(R14_q),
    .in15(R15_q), .out(ReadData2), .sel(ReadRg2_Rt));
endmodule

module Control_Unit (
  input  [3:0] in_1,
  output ReqWriteEN,
  output Rt_Im,
  output Bin,
  output Cin,
  output [1:0] Opcode,
  output MEMToReq,
  output Branch,
  output Load,
  output Store,
  output Jump
);

  wire ADD0101_out, ADDI0001_out, AND0111_out, SLL0100_out, SLT0011_out, SUB0010_out;

  and BEQ0000 (Branch, ~in_1[3], ~in_1[2], ~in_1[1], ~in_1[0]);  // AND_Gate
  and ADDI0001 (ADDI0001_out, ~in_1[3], ~in_1[2], ~in_1[1], in_1[0]);  // AND_Gate
  and SUB0010 (SUB0010_out, ~in_1[3], ~in_1[2], in_1[1], ~in_1[0]);  // AND_Gate
  and SLL0100 (SLL0100_out, ~in_1[3], in_1[2], ~in_1[1], ~in_1[0]);  // AND_Gate
  and SLT0011 (SLT0011_out, ~in_1[3], ~in_1[2], in_1[1], in_1[0]);  // AND_Gate
  and ADD0101 (ADD0101_out, ~in_1[3], in_1[2], ~in_1[1], in_1[0]);  // AND_Gate
  and LW0110 (Load, ~in_1[3], in_1[2], in_1[1], ~in_1[0]);  // AND_Gate
  and AND0111 (AND0111_out, ~in_1[3], in_1[2], in_1[1], in_1[0]);  // AND_Gate
  and JMP1000 (Jump, in_1[3], ~in_1[2], ~in_1[1], ~in_1[0]);  // AND_Gate
  and SW1001 (Store, ~in_1[3], in_1[2], ~in_1[1], in_1[0]);  // AND_Gate
  or or_1 (ReqWriteEN, ADDI0001_out, SUB0010_out, SLT0011_out, SLL0100_out, ADD0101_out, AND0111_out, Store);
  or or_2 (Rt_Im, ADDI0001_out, Load, Jump, Store);
  or or_3 (Bin, Branch, SUB0010_out);
  or or_4 (Cin, Branch, SUB0010_out);
  or or_5 (Opcode[0], Branch, ADDI0001_out, SUB0010_out, SLL0100_out, ADD0101_out, Load, Store);
  or or_6 (Opcode[1], Branch, ADDI0001_out, SUB0010_out, ADD0101_out, Load, Store);

  assign MEMToReq = Load;
endmodule

module DataPath (
  output [3:0] Opcode,
  output [3:0] Rd,
  output out_3,
  output [3:0] Rs,
  output [3:0] Rt_Im,
  output [15:0] Result
);

  wire and_1_out, clock_1_out, control_unit_1_bin, control_unit_1_branch, control_unit_1_cin,
       control_unit_1_jump, control_unit_1_load, control_unit_1_memtoreq, control_unit_1_reqwriteen,
       control_unit_1_rt_im, control_unit_1_store, n16bit_alu_1_zero;
  wire [1:0] control_unit_1_opcode;
  wire [15:0] adder_1_out, adder_2_out, bit_extender_1_out, bit_extender_2_out, counter_1_q,
       multiplexer_1_out, multiplexer_2_out, multiplexer_3_out, n16bit_alu_1_result,
       n16bit_register_1_readdata1, n16bit_register_1_readdata2, ram_1_data;

  Counter #(.width(16), .max('hffff)) counter_1 (
    .D(multiplexer_3_out), .Q(counter_1_q), .clk(clock_1_out));  // open: load, count, carry, clr
  Clock clock_1 (.out(clock_1_out));
  Adder #(.width(16)) adder_1 (.a(counter_1_q), .b(16'h1), .out(adder_1_out), .cin(1'b0));  // open: cout
  ROM #(.addrWidth(16), .dataWidth(16)) rom_1 (.addr(counter_1_q), .data({Opcode, Rd, Rs, Rt_Im}));  // open: sel
  Control_Unit control_unit_1 (
    .in_1(Opcode), .ReqWriteEN(control_unit_1_reqwriteen), .Rt_Im(control_unit_1_rt_im),
    .Bin(control_unit_1_bin), .Cin(control_unit_1_cin), .MEMToReq(control_unit_1_memtoreq),
    .Branch(control_unit_1_branch), .Load(control_unit_1_load), .Store(control_unit_1_store),
    .Opcode(control_unit_1_opcode), .Jump(control_unit_1_jump));
  assign bit_extender_1_out = {{12{1'b0}}, Opcode};  // Bit_Extender bit_extender_1
  assign bit_extender_2_out = {{4{1'b0}}, {Rd, Rs, Rt_Im}};  // Bit_Extender bit_extender_2
  _16bit_Register u_16bit_register_1 (
    .Write_Data(Result), .ReadReg1_Rs(Rs), .RegWriteEN(control_unit_1_reqwriteen), .Write_Select_Rd(Rd),
    .ReadRg2_Rt(Opcode), .CLK(clock_1_out), .ReadData1(n16bit_register_1_readdata1),
    .ReadData2(n16bit_register_1_readdata2));
  Adder #(.width(16)) adder_2 (.a(adder_1_out), .b(bit_extender_1_out), .out(adder_2_out));  // open: cin, cout
  Multiplexer #(.width(16), .enable("false")) multiplexer_1 (
    .in0(n16bit_register_1_readdata2), .in1(bit_extender_1_out), .out(multiplexer_1_out),
    .sel(control_unit_1_rt_im));
  _16bit_ALU u_16bit_alu_1 (
    .Cin(control_unit_1_cin), .A(n16bit_register_1_readdata1), .Opcode(control_unit_1_opcode),
    .B(multiplexer_1_out), .Bin(control_unit_1_bin), .Cout(out_3), .Result(n16bit_alu_1_result),
    .Zero(n16bit_alu_1_zero));
  and and_1 (and_1_out, n16bit_alu_1_zero, control_unit_1_branch);
  Multiplexer #(.width(16), .enable("false")) multiplexer_2 (
    .in0(adder_1_out), .in1(adder_2_out), .out(multiplexer_2_out), .sel(and_1_out));
  Multiplexer #(.width(16), .enable("false")) multiplexer_3 (
    .in0(multiplexer_2_out), .in1(bit_extender_2_out), .out(multiplexer_3_out), .sel(control_unit_1_jump));
  RAM #(.addrWidth(16), .dataWidth(16), .bus("separate")) ram_1 (
    .addr(n16bit_alu_1_result), .din(n16bit_register_1_readdata2), .data(ram_1_data),
    .str(control_unit_1_store), .clk(clock_1_out), .ld(control_unit_1_load));  // open: sel, clr
  Multiplexer #(.width(16), .enable("false")) multiplexer_4 (
    .in0(n16bit_alu_1_result), .in1(ram_1_data), .out(Result), .sel(control_unit_1_memtoreq));

  // Notes on the sheet:
  //   contents of rom_1 (hex, n*v repeats v):
  //   2122 1113 2444 1442 4514
endmodule
